// Logisim project G2.circ as structural Verilog: 4 circuits, main circuit main
module main (
  output [5:0] out_1,
  output [3:0] out_2,
  output [1:0] out_3
);

  wire ALUSrc, and_1_out, Branch, Jump, MemRead, MemtoReg, MemWrite, mips_alu_1_p4, RegDst,
       registerfile_1_p7, RegWrite, Tick;
  wire [3:0] alu_control_1_out_2, mips_alu_1_p3;
  wire [4:0] if_id_1_inst___out_3, multiplexer_2_out, multiplexer_3_out;
  wire [5:0] if_id_1_inst___out_4;
  wire [9:0] if_id_1_inst___out;
  wire [20:16] if_id_1_inst___out_2;
  wire [23:0] bit_extender_4_out;
  wire [27:0] bit_extender_1_out, if_id_1_pc__out;
  wire [31:0] adder_1_p3, adder_2_p4, adder_3_p3, bit_extender_2_out, bit_extender_3_out, if_id_1_pc__out_2,
       mips_alu_1_p5, mips_ram_1_p6, mipsprogramrom_1_p1, multiplexer_1_out, multiplexer_4_out,
       multiplexer_5_out, multiplexer_7_out, multiplexer_8_out, multiplexer_9_out, PC_q, registerfile_1_p8,
       shifter_2_out, shifter_3_out;

  Clock clock_1 (.out(Tick));
  Register #(.width(32)) PC (.D(multiplexer_8_out), .Q(PC_q), .clk(Tick));  // open: en, clr
  // Adder adder_1: pin names not known; wires that end beside it: PC_q, 32'h4, adder_1_p3
  // Adder adder_2: pin names not known; wires that end beside it: PC_q, 32'h8, PC_q, adder_2_p4
  IF_ID if_id_1 (
    .Clock(Tick), .PC__in(adder_1_p3), .Inst___in(mipsprogramrom_1_p1),
    .PC__out({if_id_1_pc__out_2[3:0], if_id_1_pc__out}),
    .Inst___out({out_1, if_id_1_inst___out_3, if_id_1_inst___out_2, if_id_1_inst___out, if_id_1_inst___out_4}));
  // MIPSProgramROM mipsprogramrom_1: pin names not known; wires that end beside it: mipsprogramrom_1_p1
  // PLA Control: pin names not known; wires that end beside it: out_1
  assign bit_extender_1_out = {{2{1'b0}}, {if_id_1_inst___out_3, if_id_1_inst___out_2, if_id_1_inst___out, if_id_1_inst___out_4}};  // Bit_Extender bit_extender_1
  assign bit_extender_2_out = {{6{1'b0}}, {if_id_1_inst___out_3, if_id_1_inst___out_2, if_id_1_inst___out, if_id_1_inst___out_4}};  // Bit_Extender bit_extender_2
  Multiplexer #(.width(32), .enable("false")) multiplexer_1 (
    .in0(multiplexer_9_out), .in1(adder_2_p4), .out(multiplexer_1_out), .sel(Jump));
  Shifter #(.width(28)) shifter_1 (.in(bit_extender_1_out), .\dist (5'b00010), .out(if_id_1_pc__out_2[31:4]));
  Shifter #(.width(32)) shifter_2 (.in(bit_extender_2_out), .\dist (5'b00010), .out(shifter_2_out));
  Multiplexer #(.width(5), .enable("false")) multiplexer_2 (
    .in0(multiplexer_3_out), .in1({5{1'b1}}), .out(multiplexer_2_out), .sel(Jump));
  Multiplexer #(.width(5), .enable("false")) multiplexer_3 (
    .in0(if_id_1_inst___out_2), .in1(if_id_1_inst___out[9:5]), .out(multiplexer_3_out), .sel(RegDst));
  assign bit_extender_3_out = {{16{if_id_1_inst___out[9]}}, {if_id_1_inst___out, if_id_1_inst___out_4}};  // Bit_Extender bit_extender_3
  Multiplexer #(.width(32), .enable("false")) multiplexer_4 (
    .in0(if_id_1_pc__out_2), .in1(shifter_2_out), .out(multiplexer_4_out), .sel(RegWrite));
  // RegisterFile registerfile_1: pin names not known; wires that end beside it: multiplexer_1_out, Tick, RegWrite, multiplexer_2_out, if_id_1_inst___out_3, if_id_1_inst___out_2, registerfile_1_p7, registerfile_1_p8
  ALU_control alu_control_1 (.in_1({out_3, if_id_1_inst___out_4}), .out_2(alu_control_1_out_2));
  Multiplexer #(.width(32), .enable("false")) multiplexer_5 (
    .in0(registerfile_1_p8), .in1(bit_extender_3_out), .out(multiplexer_5_out), .sel(ALUSrc));
  Shifter #(.width(32)) shifter_3 (.in(bit_extender_3_out), .\dist (5'b00010), .out(shifter_3_out));
  // MIPS_ALU mips_alu_1: pin names not known; wires that end beside it: registerfile_1_p7, multiplexer_5_out, mips_alu_1_p3, mips_alu_1_p4, mips_alu_1_p5
  Multiplexer #(.width(4), .enable("false")) multiplexer_6 (
    .in0(alu_control_1_out_2), .in1(out_2), .out(mips_alu_1_p3), .sel(alu_control_1_out_2[3]));
  Imm__Ctrl imm_ctrl_1 (.in_1(out_1[2:0]), .out_2(out_2));
  // Adder adder_3: pin names not known; wires that end beside it: {if_id_1_pc__out_2[3:0], if_id_1_pc__out}, shifter_3_out, adder_3_p3
  and and_1 (and_1_out, Branch, mips_alu_1_p4);
  Bit_Extender #(.in_width(32), .out_width(24)) bit_extender_4 (.in(mips_alu_1_p5), .out(bit_extender_4_out));
  Multiplexer #(.width(32), .enable("false")) multiplexer_7 (
    .in0({if_id_1_pc__out_2[3:0], if_id_1_pc__out}), .in1(adder_3_p3), .out(multiplexer_7_out),
    .sel(and_1_out));
  Multiplexer #(.width(32), .enable("false")) multiplexer_8 (
    .in0(multiplexer_7_out), .in1(multiplexer_4_out), .out(multiplexer_8_out), .sel(Jump));
  // MIPS_RAM mips_ram_1: pin names not known; wires that end beside it: bit_extender_4_out, registerfile_1_p8, MemWrite, MemRead, Tick, mips_ram_1_p6
  Multiplexer #(.width(32), .enable("false")) multiplexer_9 (
    .in0(mips_alu_1_p5), .in1(mips_ram_1_p6), .out(multiplexer_9_out), .sel(MemtoReg));

  // Other names for the same wires on the sheet: ALUOp[1:0] = out_3
endmodule

module ALU_control (
  input  [7:0] in_1,
  output [3:0] out_2
);

  // PLA pla_1: pin names not known; wires that end beside it: in_1, out_2
endmodule

module Imm__Ctrl (
  input  [2:0] in_1,
  output [3:0] out_2
);

  // PLA Imm__Ctrl: pin names not known; wires that end beside it: in_1, out_2
endmodule

module IF_ID (
  input  Clock,
  input  [31:0] PC__in,
  input  [31:0] Inst___in,
  output [31:0] PC__out,
  output [31:0] Inst___out
);

  Register #(.width(32)) register_1 (.D(PC__in), .Q(PC__out), .clk(Clock));  // open: en, clr
  Register #(.width(32)) register_2 (.D(Inst___in), .Q(Inst___out), .clk(Clock));  // open: en, clr

  // Other names for the same wires on the sheet: Tick = Clock
endmodule
